// Digital circuit control.dig as structural Verilog
module control (
  input  [15:0] Instr,
  input  En,
  output [3:0] RT,
  output RTW,
  output [7:0] Imm,
  output LoD
);

  wire _0_7Imm;
  wire [3:0] RT_t;
  wire [7:0] Imm_t;

  assign RT_t = _0_7Imm ? Instr[11:8] : 4'bz;  // Driver driver_1
  assign Imm_t = _0_7Imm ? Instr[7:0] : 8'bz;  // Driver driver_2
  Decoder #(.Selector_Bits(4)) decoder_1 (
    .sel(Instr[15:12]), .out_2(_0_7Imm));  // open: out_0, out_1, out_3, out_4, out_5, out_6, out_7, out_8, out_9, out_10, out_11, out_12, out_13, out_14, out_15
  and and_1 (RTW, _0_7Imm, En);
  and and_2 (LoD, _0_7Imm, En);
  assign RT = En ? RT_t : 4'bz;  // Driver driver_3
  assign Imm = En ? Imm_t : 8'bz;  // Driver driver_4

  // Other names for the same wires on the sheet: _8_11RT = _0_7Imm; LoD_t = _0_7Imm; RTW_t = _0_7Imm

  // Notes on the sheet:
  //   RT: Address of target register
  //   RTW: Address of target register
  //   Imm: 8 bit immediate value
  //   LoD: Write target with low bits set to Imm to data
  //   En: Enabled when on
endmodule
