// Digital circuit hardware.dig as structural Verilog
module hardware (
  input  clk,
  input  in_2,
  input  in_3,
  input  in_4,
  input  [15:0] in_5
);

  wire and_2_out, Clk_t, control_1_p7, control_1_p9, control_1_p10, control_1_p11, control_1_p14,
       control_1_p15, Halt, InstrEx, InstrL, jumpdecider_1_jmp, PC_ovf, rs_ff_1_nq, rs_ff_1_q, RTW,
       Un_Halt_out;
  wire [3:0] control_1_p6, control_1_p12, control_1_p16, Flags_q, RA, RT;
  wire [7:0] control_1_p8, registerfile_1_da, registerfile_1_da_2;
  wire [15:0] alu_1_rdata, driver_1_out, InstrReg_q, jumpcalc_1_npc, PC_out, ramdualport_1_d,
       registerfile_1_db;

  Button Un_Halt (.out(Un_Halt_out));
  CounterPreset #(.Bits(16)) PC (
    .en(InstrL), .C(Clk_t), .dir(in_2), .in(jumpcalc_1_npc), .ld(and_2_out), .clr(in_3), .out(PC_out),
    .ovf(PC_ovf));
  RS_FF rs_ff_1 (.S(Halt), .C(clk), .R(Un_Halt_out), .Q(rs_ff_1_q), .nQ(rs_ff_1_nq));
  Counter Phase (.en(1'b1), .C(Clk_t), .clr(1'b0), .out(InstrEx));  // open: ovf
  // Probe on PC_ovf
  and and_1 (Clk_t, rs_ff_1_nq, clk);
  not not_1 (InstrL, InstrEx);
  LED Halted (.in(rs_ff_1_q));
  LED Running (.in(Clk_t));
  RAMDualPort #(.AddrBits(16), .isProgramMemory("true"), .Bits(16)) ramdualport_1 (
    .A(PC_out), .Din(in_5), .str(in_4), .C(Clk_t), .ld(1'b1), .D(ramdualport_1_d));
  Register #(.Bits(16)) InstrReg (.D(ramdualport_1_d), .C(Clk_t), .en(InstrL), .Q(InstrReg_q));
  RegisterFile #(.AddrBits(4), .Bits(16)) registerfile_1 (
    .Din(driver_1_out), .we(RTW), .Rw(RT), .C(Clk_t), .Ra(RT), .Rb(RA),
    .Da({registerfile_1_da_2, registerfile_1_da}), .Db(registerfile_1_db));
  // Probe on InstrReg_q
  // control control_1: pin names not known; wires that end beside it: InstrReg_q, InstrEx, RT, RTW, RA, control_1_p6, control_1_p7, control_1_p8, control_1_p9, control_1_p10, control_1_p11, control_1_p12, Halt, control_1_p14, control_1_p15, control_1_p16
  alu alu_1 (
    .Op(control_1_p6), .TData({registerfile_1_da_2, registerfile_1_da}), .AData(registerfile_1_db),
    .RData(alu_1_rdata));
  assign driver_1_out = control_1_p7 ? alu_1_rdata : 16'bz;  // Driver driver_1
  jumpCalc jumpcalc_1 (
    .PC(PC_out), .Imm(control_1_p8), .Reg(registerfile_1_db), .JReg(control_1_p14), .RRel(control_1_p15),
    .nPC(jumpcalc_1_npc));
  // Probe on control_1_p8
  assign driver_1_out = control_1_p9 ? {registerfile_1_da_2, control_1_p8} : 16'bz;  // Driver driver_2
  assign driver_1_out = control_1_p10 ? {control_1_p8, registerfile_1_da} : 16'bz;  // Driver driver_3
  // Probe on driver_1_out
  Register #(.Bits(4)) Flags (.D(control_1_p16), .C(Clk_t), .en(control_1_p7), .Q(Flags_q));
  jumpDecider jumpdecider_1 (.JT(control_1_p12), .Fl(Flags_q), .Jmp(jumpdecider_1_jmp));
  LED led_1 (.in(Flags_q[0]));
  LED led_2 (.in(Flags_q[1]));
  LED led_3 (.in(Flags_q[2]));
  LED led_4 (.in(Flags_q[3]));
  and and_2 (and_2_out, control_1_p11, jumpdecider_1_jmp);

  // Notes on the sheet:
  //   clk: Hz: 20
  //   Imm
  //   Data
  //   fN
  //   fZ
  //   fC
  //   fO
endmodule
